# Fritzing sketch ESP8266_TFT18 (saved by Fritzing 0.9.2b)

parts:
  U2 = ESP8266 WiFi Module [part_number=ESP8266]
  TFT18/16p1 = tft18_16p

nets:
  VCC: U2.VCC, TFT18/16p1.Vcc
  N1: U2.GPIO_2, TFT18/16p1.LED_+
  GND: U2.GND, TFT18/16p1.GND
  N2: U2.GPIO_15, TFT18/16p1.CS#6
  N3: U2.GPIO_4, TFT18/16p1.CS#2
  N4: U2.GPIO_5, TFT18/16p1.A0
  N5: U2.GPIO_16, TFT18/16p1.RESET
  N6: U2.GPIO_14, TFT18/16p1.SCK
  N7: U2.GPIO_12, TFT18/16p1.MISO
  N8: U2.GPIO_13, TFT18/16p1.MOSI, TFT18/16p1.SDA

custom parts:
  ESP8266 WiFi Module: Generic WiFi Module based on the ESP8266 with onboard PCB antenna and UART communications
  tft18_16p: 1.8" TFT 16pin w/SD-card-slot
