# Fritzing sketch ESP8266_TFT22 (saved by Fritzing 0.9.2b)

parts:
  U2 = ESP8266 WiFi Module [part_number=ESP8266]
  JP2 = TFT 2.2" 240x320 w SD-Card slot

nets:
  VCC: U2.VCC, JP2.Vcc
  N1: U2.GPIO_2, JP2.LED
  GND: U2.GND, JP2.GND
  N2: U2.GPIO_4, JP2.CS
  N3: U2.GPIO_5, JP2.D/C
  N4: U2.GPIO_16, JP2.RESET
  N5: U2.GPIO_14, JP2.SCK
  N6: U2.GPIO_12, JP2.MISO
  N7: U2.GPIO_13, JP2.MOSI

custom parts:
  ESP8266 WiFi Module: Generic WiFi Module based on the ESP8266 with onboard PCB antenna and UART communications
  TFT 2.2" 240x320 w SD-Card slot: A Breakout board containing a TFT Display with 2.2" visible diameter, SPI driven with additional SD-Card slot - even SPI driven
