# Fritzing sketch ESP_SensorNode-ESP01-DS18B20 (saved by Fritzing 0.9.2b)
perfboards: 1
breadboards: 1

parts:
  U1 = ESP8266 WiFi Module [part_number=ESP8266]  # not connected
  DS1 = DS18B20 1-Wire Temperature Sensor Probe Cable
  R1 = Resistor [tolerance=±5% resistance=4.7k package=THT]

nets:
  N1: DS1.DQ, R1.Pin_0
  N2: DS1.VDD, R1.Pin_1

notes:
  GND
  3V3
  GPIO2
  GPIO0
  Tx
  Rx
  RST

custom parts:
  ESP8266 WiFi Module: Generic WiFi Module based on the ESP8266 with onboard PCB antenna and UART communications
