# Fritzing sketch ESP_SensorNode-Step3 (saved by Fritzing 0.9.2b)
perfboards: 1
breadboards: 1

parts:
  U1 = ESP8266 WiFi Module [part_number=ESP8266]  # not connected
  DHT1 = DHT22 Humidity and Temperature Sensor

nets:
  N1: DHT1.NULL, DHT1.GND

notes:
  GND
  3V3
  GPIO2
  GPIO0
  Tx
  Rx
  RST

custom parts:
  ESP8266 WiFi Module: Generic WiFi Module based on the ESP8266 with onboard PCB antenna and UART communications
